# Fritzing sketch ACCESS-SECURITY-FRITZ (saved by Fritzing 0.7.12b)
breadboards: 2

parts:
  U1 = Arduino Mega
  kEYPAD_MATRICIAL_1 = KEYPAD 4x3
  Nokia_5110_LCD_Module1 = Nokia5110LCDModule
  R1 = Resistor [tolerance=±5% resistance=1k package=THT]
  R2 = Resistor [tolerance=±5% resistance=10k package=THT]
  R4 = Resistor [tolerance=±5% resistance=10k package=THT]
  R5 = Resistor [tolerance=±5% resistance=10k package=THT]
  LED2 = LED - 3mm [color="Red (633nm)" package="3 mm [THT]"]
  LED1 = LED - 3mm [color="Green (555nm)" package="3 mm [THT]"]
  R6 = 100 Ω Resistor [package=THT]
  R7 = 100 Ω Resistor [package=THT]
  SPKR1 = Loudspeaker
  R8 = 150 Ω Resistor [package=THT]
  J1 = Infrared Proximity Sensor
  J2 = Infrared Proximity Sensor
  J3 = Infrared Proximity Sensor
  IR1 = TSOP312.., 314.. [package=THT]
  J4 = Basic Servo

nets:
  N1: U1.D12, J1.Vout
  N2: U1.D11, J2.Vout
  N3: U1.D10, J3.Vout
  N4: U1.D9, IR1.GND
  N5: U1.D8, R8.Pin_0
  N6: U1.D3, J4.pulse
  N7: U1.3V3, Nokia_5110_LCD_Module1.LED
  VCC: U1.+5V, SPKR1.pin1, J1.Vcc, J2.Vcc, J3.Vcc, IR1.Vs, J4.vcc
  GND: U1.GND, Nokia_5110_LCD_Module1.RST, LED2.cathode, LED1.cathode, J1.GND, J2.GND, J3.GND, IR1.Data, J4.gnd
  N8: U1.D24, R4.Pin_1
  N9: U1.D25, R5.Pin_1
  N10: U1.D26, R2.Pin_1
  N11: U1.D27, Nokia_5110_LCD_Module1.D/C
  N12: U1.D28, R1.Pin_1
  N13: U1.D40, R7.Pin_1
  N14: U1.D41, R6.Pin_1
  N15: U1.D42, kEYPAD_MATRICIAL_1.arrow2
  N16: U1.D43, kEYPAD_MATRICIAL_1.arrow3
  N17: U1.D44, kEYPAD_MATRICIAL_1.arrow4
  N18: U1.D45, kEYPAD_MATRICIAL_1.arrow1
  N19: U1.D46, kEYPAD_MATRICIAL_1.col3
  N20: U1.D47, kEYPAD_MATRICIAL_1.col1
  N21: U1.D48, kEYPAD_MATRICIAL_1.col2
  N22: Nokia_5110_LCD_Module1.Vcc, R4.Pin_0
  N23: Nokia_5110_LCD_Module1.CS, R1.Pin_0
  N24: Nokia_5110_LCD_Module1.DIN, R2.Pin_0
  N25: Nokia_5110_LCD_Module1.CLK, R5.Pin_0
  N26: LED2.anode, R6.Pin_0
  N27: LED1.anode, R7.Pin_0
  N28: SPKR1.pin2, R8.Pin_1

custom parts:
  KEYPAD 4x3: KEYPAD matricial de 12 botones, 4 filas x 3 columnas
  : Nokia 5110 LCD with 8 pin. It's a 1.94in*1.66in module part. Description: The Nokia 5110 is a basic graphic LCD screen for lots of applications. It was originally intended for as a cell phone screen. This one is mounted on an easy to solder PCB. It uses the PCD8544 controller. The PCD8544 is a low power CMOS LCD controller/driver, designed to drive a graphic display of 48 rows and 84 columns.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
