# Fritzing sketch Luminosity-RGB (saved by Fritzing 0.7.12b)
breadboards: 1

parts:
  U1 = Arduino Mega
  Q1 = Basic FET N-Channel [package="TO220 [THT]"]
  Q2 = Basic FET N-Channel [package="TO220 [THT]"]
  Q3 = Basic FET N-Channel [package="TO220 [THT]"]
  R1 = 1k Ω Resistor [package=THT]
  R2 = 1k Ω Resistor [package=THT]
  R3 = 1k Ω Resistor [package=THT]
  R4 = Photocell (LDR) [package=THT]
  R5 = 1k Ω Resistor [package=THT]
  LED1 = RGB LED - (4 legs) [package="5 mm [THT]"]

nets:
  N1: U1.D11, Q3.gate
  N2: U1.D10, Q2.gate
  N3: U1.D9, Q1.gate
  N4: U1.+5V, R5.Pin_1
  N5: U1.GND, R4.pin_1
  N6: U1.VIN, LED1.blue_cathode
  N7: U1.A0, R4.pin_0, R5.Pin_0
  N8: Q1.drain, LED1.red_cathode
  N9: Q1.source, Q2.source, Q3.source, R1.Pin_0, R1.Pin_1, R2.Pin_0, R2.Pin_1, R3.Pin_0, R3.Pin_1
  N10: Q2.drain, LED1.common_anode
  N11: Q3.drain, LED1.green_cathode

notes:
  Dimmable LED Strip Light High Brightness w/ 5050 LEDs, 60/m, by 5-meter reel ( Infra Red 850 nm)
  irrf850-5050-60-reel
  850 nm/5050-60
  MUST PLUG A 12V POWER SOURCE here >>>>>>
