# Fritzing sketch temperature-fan (saved by Fritzing 0.7.12b)
breadboards: 1

parts:
  U1 = Arduino Mega
  Q1 = Basic FET N-Channel [package="TO220 [THT]"]
  R1 = 1k Ω Resistor [package=THT]
  D1 = Schottky Diode [part_number=1N5817 package="Melf DO-213 AB [SMD]"]
  M1 = DC Motor
  Q2 = Temperature sensor [package="TO92 [THT]"]
  R2 = Resistor [tolerance=±5% resistance=4.7k package="0805 [SMD]"]

nets:
  GND: U1.GND, Q1.source, R1.Pin_1, Q2.GND
  VIN: U1.VIN, D1.cathode, M1.pin_1, Q2.Vdd, R2.Pin_0
  N1: U1.D32, Q2.DQ, R2.Pin_1
  N2: U1.D33, Q1.gate, R1.Pin_0
  N3: Q1.drain, D1.anode, M1.pin_2

custom parts:
  Temperature sensor: Dellas temperature sensor
