# Fritzing sketch TemperatureSensor_RHT03_2Coolers_motionSensor (saved by Fritzing 0.7.12b)
breadboards: 1

parts:
  U1 = Arduino Mega
  R2 = Resistor [tolerance=±5% resistance=10k package=THT]
  R3 = Resistor [tolerance=±5% resistance=10k package=THT]
  RHT04 = Humidity and Temperature Sensor RHT03
  IR_Reciever_(TSOP22)1 = IR Reciever
  R4 = Resistor [tolerance=±5% resistance=330 package=THT]
  LED1 = LED - 3mm [color="Red (633nm)" package="3 mm [THT]"]
  M1 = DC Motor
  M2 = DC Motor
  R5 = Resistor [tolerance=±5% resistance=10k package=THT]
  Q2 = Basic FET N-Channel [package="TO220 [THT]"]
  Q1 = Basic FET N-Channel [package="TO220 [THT]"]

nets:
  N1: U1.D13, R2.Pin_1
  N2: U1.D12, R5.Pin_1
  N3: U1.D7, R3.Pin_0, RHT04.Data-signal
  N4: U1.D6, IR_Reciever_(TSOP22)1.Vs
  N5: U1.D5, LED1.cathode
  +5V: U1.+5V, R3.Pin_1, RHT04.Vcc, IR_Reciever_(TSOP22)1.OUT
  GND: U1.GND, IR_Reciever_(TSOP22)1.GND, R4.Pin_1
  N6: U1.VIN, M1.pin_1, M2.pin_1
  N7: R2.Pin_0, Q1.gate
  N8: RHT04.GND_2, Q2.source, Q1.source
  N9: R4.Pin_0, LED1.anode
  N10: M1.pin_2, Q1.drain
  N11: M2.pin_2, Q2.drain
  N12: R5.Pin_0, Q2.gate

custom parts:
  Humidity and Temperature Sensor RHT03: Digital relative humidity & temperature sensor RHT03
  IR Reciever: Basic infrared reciever
