# Fritzing sketch keypad_unlocker_fritz (saved by Fritzing 0.7.12b)
breadboards: 1

parts:
  U1 = Arduino Mega
  kEYPAD_MATRICIAL_1 = KEYPAD 4x3
  LED1 = green LED - 5mm
  R1 = Resistor [tolerance=±5% resistance=100 package="0603 [SMD]"]
  R2 = Resistor [tolerance=±5% resistance=100 package="0603 [SMD]"]
  LED2 = yellow LED - 5mm

nets:
  N1: U1.GND, LED1.cathode, LED2.cathode
  N2: U1.D42, kEYPAD_MATRICIAL_1.col2
  N3: U1.D43, kEYPAD_MATRICIAL_1.col1
  N4: U1.D44, kEYPAD_MATRICIAL_1.col3
  N5: U1.D45, kEYPAD_MATRICIAL_1.arrow1
  N6: U1.D46, kEYPAD_MATRICIAL_1.arrow4
  N7: U1.D47, kEYPAD_MATRICIAL_1.arrow3
  N8: U1.D48, kEYPAD_MATRICIAL_1.arrow2
  N9: U1.D52, R2.Pin_0
  N10: U1.D53, R1.Pin_0
  N11: LED1.anode, R2.Pin_1
  N12: R1.Pin_1, LED2.anode

notes:
  OBS: Wire colors
  Yellow and White are columns
  Green and Blue are lines

custom parts:
  KEYPAD 4x3: KEYPAD matricial de 12 botones, 4 filas x 3 columnas
