# Fritzing sketch LCD_NOKIA_3310_e_KEYPAD (saved by Fritzing 0.7.12b)
breadboards: 1

parts:
  U1 = Arduino Mega
  kEYPAD_MATRICIAL_1 = KEYPAD 4x3
  Nokia_5110_LCD_Module1 = Nokia5110LCDModule
  R1 = Resistor [tolerance=±5% resistance=1k package=THT]
  R2 = Resistor [tolerance=±5% resistance=10k package=THT]
  R4 = Resistor [tolerance=±5% resistance=10k package=THT]
  R5 = Resistor [tolerance=±5% resistance=10k package=THT]
  LED2 = LED - 3mm [color="Red (633nm)" package="3 mm [THT]"]
  LED1 = LED - 3mm [color="Green (555nm)" package="3 mm [THT]"]
  R6 = 100 Ω Resistor [package=THT]
  R7 = 100 Ω Resistor [package=THT]

nets:
  N1: U1.+5V, Nokia_5110_LCD_Module1.LED
  N2: U1.GND, Nokia_5110_LCD_Module1.RST, LED2.cathode, LED1.cathode
  N3: U1.D24, R4.Pin_1
  N4: U1.D25, R5.Pin_1
  N5: U1.D26, R2.Pin_1
  N6: U1.D27, Nokia_5110_LCD_Module1.D/C
  N7: U1.D28, R1.Pin_1
  N8: U1.D42, kEYPAD_MATRICIAL_1.arrow2
  N9: U1.D43, kEYPAD_MATRICIAL_1.arrow3
  N10: U1.D44, kEYPAD_MATRICIAL_1.arrow4
  N11: U1.D45, kEYPAD_MATRICIAL_1.arrow1
  N12: U1.D46, kEYPAD_MATRICIAL_1.col3
  N13: U1.D47, kEYPAD_MATRICIAL_1.col1
  N14: U1.D48, kEYPAD_MATRICIAL_1.col2
  N15: U1.D52, R7.Pin_1
  N16: U1.D53, R6.Pin_1
  N17: Nokia_5110_LCD_Module1.Vcc, R4.Pin_0
  N18: Nokia_5110_LCD_Module1.CS, R1.Pin_0
  N19: Nokia_5110_LCD_Module1.DIN, R2.Pin_0
  N20: Nokia_5110_LCD_Module1.CLK, R5.Pin_0
  N21: LED2.anode, R6.Pin_0
  N22: LED1.anode, R7.Pin_0

custom parts:
  KEYPAD 4x3: KEYPAD matricial de 12 botones, 4 filas x 3 columnas
  : Nokia 5110 LCD with 8 pin. It's a 1.94in*1.66in module part. Description: The Nokia 5110 is a basic graphic LCD screen for lots of applications. It was originally intended for as a cell phone screen. This one is mounted on an easy to solder PCB. It uses the PCD8544 controller. The PCD8544 is a low power CMOS LCD controller/driver, designed to drive a graphic display of 48 rows and 84 columns.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
