# Fritzing sketch sensorPresenca (saved by Fritzing 0.7.12b)
breadboards: 1

parts:
  U1 = Arduino Mega
  SPKR1 = Loudspeaker
  R1 = 150k Ω Resistor [package=THT]
  J1 = Infrared Proximity Sensor  # not connected

nets:
  N1: U1.D8, R1.Pin_0
  N2: SPKR1.pin2, R1.Pin_1

notes:
  SensorPresence
